// Digital circuit cpu.dig as structural Verilog
module cpu (
  input  in_1,
  input  in_2,
  input  in_3,
  input  in_4,
  input  in_5
);

  wire IC_o_0, IC_o_1, IC_o_2, IC_o_3, madr_q_0, madr_q_1, madr_q_2, madr_q_3, memory2_1_o_0, memory2_1_o_1,
       memory2_1_o_2, memory2_1_o_3, tri_state_buffer_4bit_1_o_0, tri_state_buffer_4bit_1_o_1,
       tri_state_buffer_4bit_1_o_2, tri_state_buffer_4bit_1_o_3;

  register_simple madr (
    .E_out(in_5), .CLK(in_4), .D_0(tri_state_buffer_4bit_1_o_0), .D_1(tri_state_buffer_4bit_1_o_1),
    .D_2(tri_state_buffer_4bit_1_o_2), .D_3(tri_state_buffer_4bit_1_o_3), .Q_0(madr_q_0), .Q_1(madr_q_1),
    .Q_2(madr_q_2), .Q_3(madr_q_3));
  memory2 memory2_1 (
    .a_0(madr_q_0), .a_1(madr_q_1), .a_2(madr_q_2), .a_3(madr_q_3), .E(in_3), .C(in_4),
    .D_0(tri_state_buffer_4bit_1_o_0), .D_1(tri_state_buffer_4bit_1_o_1), .D_2(tri_state_buffer_4bit_1_o_2),
    .D_3(tri_state_buffer_4bit_1_o_3), .O_0(memory2_1_o_0), .O_1(memory2_1_o_1), .O_2(memory2_1_o_2),
    .O_3(memory2_1_o_3));  // open: O_4, O_5, O_6, O_7
  tri_state_buffer_4bit tri_state_buffer_4bit_1 (
    .D_0(memory2_1_o_0), .D_1(memory2_1_o_1), .D_2(memory2_1_o_2), .D_3(memory2_1_o_3), .E(in_2),
    .O_0(tri_state_buffer_4bit_1_o_0), .O_1(tri_state_buffer_4bit_1_o_1), .O_2(tri_state_buffer_4bit_1_o_2),
    .O_3(tri_state_buffer_4bit_1_o_3));
  tri_state_buffer_4bit tri_state_buffer_4bit_2 (
    .D_0(IC_o_0), .D_1(IC_o_1), .D_2(IC_o_2), .D_3(IC_o_3), .E(in_1), .O_0(tri_state_buffer_4bit_1_o_0),
    .O_1(tri_state_buffer_4bit_1_o_1), .O_2(tri_state_buffer_4bit_1_o_2), .O_3(tri_state_buffer_4bit_1_o_3));
  counter IC (.C(in_4), .O_0(IC_o_0), .O_1(IC_o_1), .O_2(IC_o_2), .O_3(IC_o_3));
endmodule
